# Fritzing sketch main (saved by Fritzing 1.0.6)
breadboards: 2

parts:
  VCC1 = Battery [internal_resistance=0.1Ω]  # not connected
  Mod1 = Raspberry Pi 4B  # not connected
  Part1 = LCD1602-I2C
  Part2 = Arduino Uno (Rev3)  # not connected
  Pololu_A1 = Pololu A4988 [package=SO16]  # not connected
  Mod2 = E3F-DS30C4 [package=THT]
  M1 = Stepper Motor - Bipolar
  R1 = Resistor [tolerance=±5% resistance=22 package="0805 [SMD]"]
  LED2 = smd LED [color="Red (633nm)" current=0.5A package="0603 [SMD]"]
  VCC2 = Battery block 9V [internal_resistance=0.1Ω]  # not connected
  AM1 = Multimeter (Ohmmeter)  # not connected
  Arduino_CNC_Shield_V3_00_1 = Arduino_CNC_V3.00
  M2 = DC Motor [voltage_(max)=12V voltage_(min)=3V]
  Mod3 = L298N DC motor driver
  VCC3 = Battery block 9V [internal_resistance=0.1Ω]
  R2 = Rotary Potentiometer (Large) [maximum_resistance=100kΩ knob_status=50% power=0.5W package=THT]
  J1 = Basic Servo  # not connected

nets:
  N1: Part1.GND, Arduino_CNC_Shield_V3_00_1.GND#76
  N2: Part1.VCC, Arduino_CNC_Shield_V3_00_1.5V#75
  N3: Part1.SDA, Arduino_CNC_Shield_V3_00_1.SDA
  N4: Part1.SCL, Arduino_CNC_Shield_V3_00_1.SCL_/_Probe
  N5: Mod2.pin1, Arduino_CNC_Shield_V3_00_1.POWER_+, Mod3.12V, VCC3.+
  N6: Mod2.pin2, Arduino_CNC_Shield_V3_00_1.End_Stops_Y+_(Gnd)
  N7: Mod2.pin3, Arduino_CNC_Shield_V3_00_1.End_Stops_Y+_(and_Y-)
  N8: M1.A, Arduino_CNC_Shield_V3_00_1.X-MTR_'1'
  N9: M1.C, Arduino_CNC_Shield_V3_00_1.X-MTR_'2'
  N10: M1.B, Arduino_CNC_Shield_V3_00_1.X-MTR_'3'
  N11: M1.D, Arduino_CNC_Shield_V3_00_1.X-MTR_'4'
  N12: R1.Pin_1, LED2.anode
  N13: Arduino_CNC_Shield_V3_00_1.EN(able), Arduino_CNC_Shield_V3_00_1.GND#2
  N14: Arduino_CNC_Shield_V3_00_1.5V#11, R2.leg2
  N15: Arduino_CNC_Shield_V3_00_1.GND#12, R2.leg1
  N16: Arduino_CNC_Shield_V3_00_1.POWER_-, Mod3.GND, VCC3.-
  N17: Arduino_CNC_Shield_V3_00_1.End_Stops_Z+_(and_Z-)_/_SpnEn, Mod3.ENA
  N18: Arduino_CNC_Shield_V3_00_1.SpnDir, Mod3.IN2
  N19: Arduino_CNC_Shield_V3_00_1.SpnDir_(Gnd), Mod3.IN1
  N20: Arduino_CNC_Shield_V3_00_1.Hold, R2.wiper
  N21: M2.pin_1, Mod3.OUT2
  N22: M2.pin_2, Mod3.OUT1

custom parts:
  LCD1602-I2C: A standard character display, usually with 2x16 characters. Comes in many colors with LCM1602 IIC attached.
  E3F-DS30C4: Omron E3F-DS30C4 Infrared Proximity Sensor module. 0 30CM (adjustable) range 6-36V NPN NO output
  Arduino_CNC_V3.00: Protoneer Arduino CNC Shield V3.00 If using Grbl V0.9: The “A” axis can not be used (yet). The “SCL” (Arduino A5) pin is now used for 'Probing' input. The “End Stops Z+ & Z-” (Arduino D11) and “SpnEn” (Arduino D12) have been switched!
  L298N DC motor driver: 2x DC motor driver with 78M05 positive voltage regulator (7..35 V) L298N: max 46 V, 2 A Set 5 V Enable jumper to enable 5 V regultor (needed for the L298N) and +5 V output at screw terminal or supply external +5 V at screw terminal Set ENA and/or ENB to +5 V to enable motor permanently or supply ENA and/or ENB with PWM signal IN1 and IN2 set rotation directory for motor A (OUT1/OUT2) IN2 and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
